# Fritzing sketch google-plant (saved by Fritzing 0.9.5d)
breadboards: 1

parts:
  R1 = Photocell (LDR) [package=THT]
  Capacitive_Soil_Moisture_Sensor1 = DFRobot Capacitive Soil Moisture Sensor V1.0 [part_number=SEN0193]
  M1 = DOIT Esp32 DevKit v1 (30 pins long, 11 pins width) [part_number=ESP32S-PIN30]
  Part1 = KY-016 RGB Full Color LED Module [package="Breakout board"]
  R2 = Resistor [tolerance=±5% resistance=10k package=THT]
  J1 = female pin header, 1 pin [form="♀ (female)"]  # not connected
  J2 = female pin header, 1 pin [form="♀ (female)"]  # not connected
  J3 = female pin header, 1 pin [form="♀ (female)"]  # not connected
  J6 = female pin header, 1 pin [form="♀ (female)"]  # not connected

nets:
  N1: R1.pin_0, M1.3V3
  N2: R1.pin_1, M1.VP, R2.Pin_1
  N3: Capacitive_Soil_Moisture_Sensor1.A, M1.VN
  VCC: Capacitive_Soil_Moisture_Sensor1.VCC, M1.VIN
  GND: Capacitive_Soil_Moisture_Sensor1.GND, M1.GND, M1.D33, Part1.-, R2.Pin_0
  N4: M1.D27, Part1.B
  N5: M1.D14, Part1.G
  N6: M1.D12, Part1.R

custom parts:
  DFRobot Capacitive Soil Moisture Sensor V1.0: DFRobot Capacitive Soil Moisture Sensor V1.0 This product measures soil moisture levels by capacitive sensing, rather than resistive sensing like other types of moisture sensor. It is made of a corrosion resistant material giving it a long service life. Insert it into soil and impress your friends with the real-time soil moisture data! The product includes an on-board voltage regulator which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
  DOIT Esp32 DevKit v1 (30 pins long, 11 pins width): The DOIT Esp32 DevKit v1 is one of the development board created by DOIT to evaluate the ESP-WROOM-32 module. It is based on the ESP32 microcontroller that boasts Wifi, Bluetooth, Ethernet and Low Power support all in a single chip. (vanepp) made breadboard work, adjusted pin numbering and labels and reduced size of schematic and cleaned up pcb. This chip is 30pins long (2 x15) and 11 pins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
  KY-016 RGB Full Color LED Module: KY-016 Arduino full color 5mm RGB LED, different colors can be obtained by mixing the three primary colors.
